# Fritzing sketch Basic_LED (saved by Fritzing 0.8.7b)
circuit board: 6.40641cm x 5.55977cm
breadboards: 1

parts:
  R1 = Resistor [tolerance=±5% resistance=330 package=THT]
  LED1 = LED - 5mm [color="Red (633nm)" package="5 mm [THT]"]
  Arduino1 = Arduino Uno (Rev3)
  part = Arduino Uno (Rev3)  # not connected

nets:
  N1: R1.Pin_0, LED1.cathode
  N2: R1.Pin_1, Arduino1.GND
  N3: LED1.anode, Arduino1.D13/SCK

notes:
  Fun with Arduino by Rob Purser is licensed under a
  Creative Commons
  Attribution-NonCommercial-ShareAlike 3.0 Unported License.
  Based on a work at https://sites.google.com/site/funarduino/
