# Fritzing sketch Audio_Light_Show_AtHome_Solution (saved by Fritzing 0.8.7b)
breadboards: 1

parts:
  Part1 = Arduino Uno (Rev3)
  R1 = Basic Flex Resistor
  R2 = Resistor [tolerance=±5% resistance=10k package=THT]
  J1 = Piezo Speaker
  R4 = Resistor [tolerance=±5% resistance=10k package=THT]  # not connected
  LED1 = LED - 5mm [color="Red (633nm)" package="5 mm [THT]"]
  LED2 = LED - 5mm [color="Red (633nm)" package="5 mm [THT]"]
  LED3 = LED - 5mm [color="Red (633nm)" package="5 mm [THT]"]
  R5 = Resistor [tolerance=±5% resistance=220 package=THT]
  R6 = Resistor [tolerance=±5% resistance=220 package=THT]
  R7 = Resistor [tolerance=±5% resistance=220 package=THT]

nets:
  N1: Part1.A0, R1.Pin_2, R2.Pin_0
  N2: Part1.D8, R6.Pin_1
  N3: Part1.D9_PWM, R7.Pin_1
  GND: Part1.GND, R1.pin_1, J1.pin1, LED1.cathode, LED2.cathode
  N4: Part1.D6_PWM, J1.pin2
  N5: Part1.D7, R5.Pin_1
  5V: Part1.5V, R2.Pin_1
  N6: LED1.anode, R6.Pin_0
  N7: LED2.anode, R7.Pin_0
  N8: LED3.anode, R5.Pin_0

notes:
  Fun with Arduino by Rob Purser is licensed under a
  Creative Commons
  Attribution-NonCommercial-ShareAlike 3.0 Unported License.
  Based on a work at https://sites.google.com/site/funarduino/
  Copyright 2013-2014, Rob Purser
  Fun with Arduino by Rob Purser is licensed under a
  Creative Commons
  Attribution-NonCommercial-ShareAlike 3.0 Unported License.
  Based on a work at https://sites.google.com/site/funarduino/
  Copyright 2013, Rob Purser
  This is really a magnetic buzzer
