# Fritzing sketch Flexpot_Buzzer (saved by Fritzing 0.8.5b)
breadboards: 1

parts:
  Part1 = Arduino Uno (Rev3)
  R1 = Basic Flex Resistor
  R2 = Resistor [tolerance=±5% resistance=10k package=THT]
  J1 = Piezo Speaker

nets:
  N1: Part1.A0, R1.Pin_2, R2.Pin_0
  GND: Part1.GND, R1.pin_1, J1.pin1
  N2: Part1.D6_PWM, J1.pin2
  5V: Part1.5V, R2.Pin_1

notes:
  Fun with Arduino by Rob Purser is licensed under a
  Creative Commons
  Attribution-NonCommercial-ShareAlike 3.0 Unported License.
  Based on a work at https://sites.google.com/site/funarduino/
  Copyright 2013-2014, Rob Purser
  Fun with Arduino by Rob Purser is licensed under a
  Creative Commons
  Attribution-NonCommercial-ShareAlike 3.0 Unported License.
  Based on a work at https://sites.google.com/site/funarduino/
  Copyright 2013, Rob Purser
  This is really a magnetic buzzer
