# Fritzing sketch SoftPot_Buzzer (saved by Fritzing 0.8.5b)
breadboards: 1

parts:
  Part1 = Arduino Uno (Rev3)
  R2 = Resistor [tolerance=±5% resistance=10k package=THT]
  J1 = Piezo Speaker
  R3 = SoftPot Potentiometer 200mm

nets:
  N1: Part1.A0, R2.Pin_1, R3.wiper
  GND: Part1.GND, R2.Pin_0, J1.pin1, R3.leg1
  N2: Part1.D6_PWM, J1.pin2
  5V: Part1.5V, R3.leg2

notes:
  Fun with Arduino by Rob Purser is licensed under a
  Creative Commons
  Attribution-NonCommercial-ShareAlike 3.0 Unported License.
  Based on a work at https://sites.google.com/site/funarduino/
  Copyright 2013-2014, Rob Purser
  This is really a magnetic buzzer
  This is a custom part
  that is in the GitHub repository
  Credit: https://code.google.com/p/fritzing/issues/detail?id=875#c510

custom parts:
  SoftPot Potentiometer 200mm: These are very thin variable potentiometers. By pressing down on various parts of the strip, the resistance linearly changes from 100Ohms to 10,000Ohms allowing the user to very accurately calculate the relative position on the strip. Can be used as an accurate positional indicator for CNC head positioning, variable user input (volume level input for example), straight user input (multiple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
