# Fritzing sketch LCD_Temp_Homework_Solution (saved by Fritzing 0.8.7b)
breadboards: 1

parts:
  R1 = Trimmer Potentiometer [maximum_resistance=10kΩ package=THT]
  LCD1 = LCD screen
  Arduino1 = Arduino Uno (Rev3)
  U1 = TMP36 [package=to-92]
  S1 = Pushbutton [package="[THT]"]
  S2 = Pushbutton [package="[THT]"]

nets:
  5V: R1.leg1, LCD1.VDD, LCD1.LED+, Arduino1.5V, U1.VCC
  N1: R1.wiper, LCD1.V0
  GND: R1.leg2, LCD1.VSS, LCD1.R/W, LCD1.LED-, Arduino1.GND, U1.GND, S1.Pin_3, S1.Pin_4, S2.Pin_3, S2.Pin_4
  N2: LCD1.RS, Arduino1.D12/MISO
  N3: LCD1.E, Arduino1.D13/SCK
  N4: LCD1.DB4, Arduino1.D5_PWM
  N5: LCD1.DB5, Arduino1.D4
  N6: LCD1.DB6, Arduino1.D3_PWM
  N7: LCD1.DB7, Arduino1.D2
  N8: Arduino1.A0, U1.VOUT
  N9: Arduino1.D8, S1.Pin_1, S1.Pin_2
  N10: Arduino1.D9_PWM, S2.Pin_1, S2.Pin_2

notes:
  Fun with Arduino by Rob Purser is licensed under a
  Creative Commons
  Attribution-NonCommercial-ShareAlike 3.0 Unported License.
  Based on a work at https://sites.google.com/site/funarduino/
  Copyright 2013-2014, Rob Purser
