# Fritzing sketch H_Bridge (saved by Fritzing 0.8.7b)
breadboards: 1

parts:
  M1 = DC Motor
  IC1 = H-Bridge [package=THT]
  Arduino1 = Arduino Uno (Rev3)

nets:
  N1: M1.pin_1, IC1.2Y
  N2: M1.pin_2, IC1.1Y
  5V: IC1.1_2EN, IC1.VCC1, Arduino1.5V
  N3: IC1.1A, Arduino1.D10_PWM/SS
  GND: IC1.GND2, Arduino1.GND
  N4: IC1.2A, Arduino1.D9_PWM
  N5: IC1.VCC2, Arduino1.VIN

notes:
  Fun with Arduino by Rob Purser is licensed under a
  Creative Commons
  Attribution-NonCommercial-ShareAlike 3.0 Unported License.
  Based on a work at https://sites.google.com/site/funarduino/
  Copyright 2013, Rob Purser
