# Fritzing sketch H_Bridge_Redux (saved by Fritzing 0.8.7b)
breadboards: 1

parts:
  M1 = DC Motor
  Arduino1 = Arduino Uno (Rev3)
  IC1 = H-Bridge [package=THT]

nets:
  N1: M1.pin_1, IC1.2Y
  N2: M1.pin_2, IC1.1Y
  N3: Arduino1.D9_PWM, IC1.2A
  N4: Arduino1.D10_PWM/SS, IC1.1A
  N5: Arduino1.D11_PWM/MOSI, IC1.1_2EN
  5V: Arduino1.5V, IC1.VCC1
  GND: Arduino1.GND, IC1.GND2
  N6: Arduino1.VIN, IC1.VCC2

notes:
  Fun with Arduino by Rob Purser is licensed under a
  Creative Commons
  Attribution-NonCommercial-ShareAlike 3.0 Unported License.
  Based on a work at https://sites.google.com/site/funarduino/
  Copyright 2013, Rob Purser
