# Fritzing sketch Magicians_Chassis (saved by Fritzing 0.8.7b)
breadboards: 1

parts:
  IC1 = H-Bridge [package=THT]
  M1 = DC Motor
  M2 = DC Motor
  Arduino1 = Arduino Uno (Rev3)
  Power_plug1 = Power plug
  VCC1 = 4 x AAA Battery Mount  # not connected
  part = 4 x AAA Battery Mount  # not connected

nets:
  N1: IC1.1_2EN, Arduino1.D11_PWM/MOSI
  N2: IC1.1A, Arduino1.D10_PWM/SS
  N3: IC1.1Y, M1.pin_2
  GND: IC1.GND2, IC1.GND4, Arduino1.GND, Power_plug1.GND
  N4: IC1.2Y, M1.pin_1
  N5: IC1.2A, Arduino1.D9_PWM
  VIN: IC1.VCC2, Arduino1.VIN, Power_plug1.VCC
  N6: IC1.3_4EN, Arduino1.D5_PWM
  N7: IC1.3A, Arduino1.D4
  N8: IC1.3Y, M2.pin_1
  N9: IC1.4Y, M2.pin_2
  N10: IC1.4A, Arduino1.D3_PWM
  5V: IC1.VCC1, Arduino1.5V

notes:
  Fun with Arduino by Rob Purser is licensed under a
  Creative Commons
  Attribution-NonCommercial-ShareAlike 3.0 Unported License.
  Based on a work at https://sites.google.com/site/funarduino/
  Copyright 2013-2014, Rob Purser
  We want to power the motors directly from the batteries, not from the +5V on the Arduino
  Right Wheel Motor
  Left Wheel Motor
  Connect 6v to Vin when the robot is NOT connected to the USB.
