# Fritzing sketch Magicians_Line Follower (saved by Fritzing 0.8.5b)
breadboards: 1
perfboards: 3

parts:
  IC1 = H-Bridge [package=THT]
  M1 = DC Motor
  M2 = DC Motor
  Arduino1 = Arduino Uno (Rev3)
  Power_plug1 = Power plug
  IC2 = IC, DIP package, 4 pins [chip_label=IC]
  R1 = Resistor [tolerance=±5% resistance=100 package="1206 [SMD]"]
  R5 = Resistor [tolerance=±5% resistance=10k package=THT]
  Right = Header 3 [package=molex-1x3_lock]
  R6 = Resistor [tolerance=±5% resistance=100 package="1206 [SMD]"]
  R7 = Resistor [tolerance=±5% resistance=10k package=THT]
  Center = Header 3 [package=molex-1x3_lock]
  IC3 = IC, DIP package, 4 pins [chip_label=IC]
  R8 = Resistor [tolerance=±5% resistance=100 package="1206 [SMD]"]
  R9 = Resistor [tolerance=±5% resistance=10k package=THT]
  Left = Header 3 [package=molex-1x3_lock]
  IC4 = IC, DIP package, 4 pins [chip_label=IC]
  VCC1 = 4 x AAA Battery Mount  # not connected

nets:
  N1: IC1.1_2EN, Arduino1.D11_PWM/MOSI
  N2: IC1.1A, Arduino1.D10_PWM/SS
  N3: IC1.1Y, M1.pin_2
  GND: IC1.GND2, IC1.GND4, Arduino1.GND, Power_plug1.GND, IC2.pin1, IC2.pin3, Right.3, Center.3, IC3.pin1, IC3.pin3, Left.3, IC4.pin1, IC4.pin3
  N4: IC1.2Y, M1.pin_1
  N5: IC1.2A, Arduino1.D9_PWM
  VIN: IC1.VCC2, Arduino1.VIN, Power_plug1.VCC
  N6: IC1.3_4EN, Arduino1.D5_PWM
  N7: IC1.3A, Arduino1.D4
  N8: IC1.3Y, M2.pin_1
  N9: IC1.4Y, M2.pin_2
  N10: IC1.4A, Arduino1.D3_PWM
  5V: IC1.VCC1, Arduino1.5V, R1.Pin_0, R5.Pin_0, Right.2, R6.Pin_0, R7.Pin_0, Center.2, R8.Pin_0, R9.Pin_0, Left.2
  N11: Arduino1.A0, IC2.pin2, R5.Pin_1, Right.1
  N12: Arduino1.A1, R7.Pin_1, Center.1, IC3.pin2
  N13: Arduino1.A2, R9.Pin_1, Left.1, IC4.pin2
  N14: IC2.pin4, R1.Pin_1
  N15: R6.Pin_1, IC3.pin4
  N16: R8.Pin_1, IC4.pin4

notes:
  Fun with Arduino by Rob Purser is licensed under a
  Creative Commons
  Attribution-NonCommercial-ShareAlike 3.0 Unported License.
  Based on a work at https://sites.google.com/site/funarduino/
  Copyright 2013, Rob Purser
  Copyright 2014, Tom Amlicke
  We want to power the motors directly from the batteries, not from the +5V on the Arduino
  Right Wheel Motor
  Left Wheel Motor
  Connect 6v to plug when the robot is NOT connected to the USB.
  Sparkfun Line Follower Sensors
