# Fritzing sketch FSR (saved by Fritzing 0.8.3b)
breadboards: 1

parts:
  Arduino1 = Arduino
  R4 = Resistor [tolerance=±5% resistance=10k package=THT]
  J1 = Basic Force Sensing Resistor (FSR) [package=THT]

nets:
  GND: Arduino1.GND, J1.pin_0
  N1: Arduino1.+5V, R4.Pin_1
  N2: Arduino1.A0, R4.Pin_0, J1.pin_1

notes:
  Fun with Arduino by Rob Purser is licensed under a
  Creative Commons
  Attribution-NonCommercial-ShareAlike 3.0 Unported License.
  Based on a work at http://goo.gl/NNe35.
