# Fritzing sketch Flex (saved by Fritzing 0.8.7b)
breadboards: 1

parts:
  R4 = Resistor [tolerance=±5% resistance=10k package=THT]
  part = Basic Force Sensing Resistor (FSR) [package=THT]  # not connected
  Arduino1 = Arduino Uno (Rev3)
  R5 = Basic Flex Resistor

nets:
  N1: R4.Pin_0, Arduino1.A0, R5.Pin_2
  N2: R4.Pin_1, Arduino1.5V
  N3: Arduino1.GND, R5.pin_1

notes:
  Fun with Arduino by Rob Purser is licensed under a
  Creative Commons
  Attribution-NonCommercial-ShareAlike 3.0 Unported License.
  Based on a work at http://www.funwitharduino.net
