# Fritzing sketch High_Striker (saved by Fritzing 0.8.3b)
breadboards: 1

parts:
  Arduino1 = Arduino
  R4 = Resistor [tolerance=±5% resistance=10k package=THT]
  J1 = Basic Force Sensing Resistor (FSR) [package=THT]
  LED2 = RGB LED - (4 legs) [package="5 mm [THT]"]
  R5 = Resistor [tolerance=±5% resistance=330 package=THT]
  R6 = Resistor [tolerance=±5% resistance=330 package=THT]
  R7 = Resistor [tolerance=±5% resistance=330 package=THT]

nets:
  GND: Arduino1.GND, Arduino1.A0, R4.Pin_0, J1.pin_0, J1.pin_1, LED2.common_anode
  N1: Arduino1.D11, R5.Pin_1
  N2: Arduino1.D10, R6.Pin_1
  N3: Arduino1.D9, R7.Pin_1
  N4: Arduino1.+5V, R4.Pin_1
  N5: LED2.red_cathode, R5.Pin_0
  N6: LED2.green_cathode, R6.Pin_0
  N7: LED2.blue_cathode, R7.Pin_0

notes:
  Fun with Arduino by Rob Purser is licensed under a
  Creative Commons
  Attribution-NonCommercial-ShareAlike 3.0 Unported License.
  Based on a work at http://goo.gl/NNe35.
