# Fritzing sketch Magicians_Chassis (saved by Fritzing 0.8.3b)
breadboards: 1

parts:
  Arduino1 = Arduino
  IC1 = H-Bridge [package=THT]
  M1 = DC Motor
  M2 = DC Motor

nets:
  GND: Arduino1.GND, IC1.GND2, IC1.GND4
  N1: Arduino1.D11, IC1.1_2EN
  N2: Arduino1.D10, IC1.1A
  N3: Arduino1.D9, IC1.2A
  N4: Arduino1.D5, IC1.3_4EN
  N5: Arduino1.D4, IC1.3A
  N6: Arduino1.D3, IC1.4A
  5V: Arduino1.+5V, IC1.VCC1
  N7: Arduino1.VIN, IC1.VCC2
  N8: IC1.1Y, M1.pin_2
  N9: IC1.2Y, M1.pin_1
  N10: IC1.3Y, M2.pin_1
  N11: IC1.4Y, M2.pin_2

notes:
  Fun with Arduino by Rob Purser is licensed under a
  Creative Commons
  Attribution-NonCommercial-ShareAlike 3.0 Unported License.
  Based on a work at https://sites.google.com/site/funarduino/
  Copyright 2013, Rob Purser
  We want to power the motors directly from the batteries, not from the +5V on the Arduino
  Right Wheel Motor
  Left Wheel Motor
