# Fritzing sketch Basic_LED (saved by Fritzing 0.8.3b)
circuit board: 6.40641cm x 5.55977cm
breadboards: 1

parts:
  Arduino1 = Arduino
  R1 = Resistor [tolerance=±5% resistance=330 package=THT]
  LED1 = LED - 5mm [color="Red (633nm)" package="5 mm [THT]"]

nets:
  N1: Arduino1.GND, R1.Pin_1
  N2: Arduino1.D13, LED1.anode
  N3: R1.Pin_0, LED1.cathode

notes:
  Fun with Arduino by Rob Purser is licensed under a
  Creative Commons
  Attribution-NonCommercial-ShareAlike 3.0 Unported License.
  Based on a work at https://sites.google.com/site/funarduino/
