# Fritzing sketch RGB_LED (saved by Fritzing 0.8.3b)
breadboards: 1

parts:
  Arduino1 = Arduino
  R1 = Resistor [tolerance=±5% resistance=330 package=THT]
  R2 = Resistor [tolerance=±5% resistance=330 package=THT]
  R3 = Resistor [tolerance=±5% resistance=330 package=THT]
  LED1 = RGB LED (com. cathode, rgb) [package="5 mm [THT]"]

nets:
  GND: Arduino1.GND, LED1.common_cathode
  N1: Arduino1.D11, R1.Pin_1
  N2: Arduino1.D10, R2.Pin_1
  N3: Arduino1.D9, R3.Pin_1
  N4: R1.Pin_0, LED1.red_anode
  N5: R2.Pin_0, LED1.green_anode
  N6: R3.Pin_0, LED1.blue_anode

notes:
  Fun with Arduino by Rob Purser is licensed under a
  Creative Commons
  Attribution-NonCommercial-ShareAlike 3.0 Unported License.
  Based on a work at https://sites.google.com/site/funarduino
  Copyright 2013, Rob Purser
