# Fritzing sketch Traffic_Light (saved by Fritzing 0.8.7b)
breadboards: 1

parts:
  R1 = Resistor [tolerance=±5% resistance=330 package=THT]
  LED1 = LED - 5mm [color="Red (633nm)" package="5 mm [THT]"]
  LED2 = LED - 5mm [color="Yellow (595nm)" package="5 mm [THT]"]
  LED3 = LED - 5mm [color="Green (570nm)" package="5 mm [THT]"]
  LED4 = LED - 5mm [color="Red (633nm)" package="5 mm [THT]"]
  LED5 = LED - 5mm [color="Yellow (595nm)" package="5 mm [THT]"]
  LED6 = LED - 5mm [color="Green (570nm)" package="5 mm [THT]"]
  R2 = Resistor [tolerance=±5% resistance=330 package=THT]
  Arduino1 = Arduino Uno (Rev3)
  part = Arduino Uno (Rev3)  # not connected

nets:
  N1: R1.Pin_0, LED1.cathode, LED2.cathode, LED3.cathode
  N2: R1.Pin_1, R2.Pin_0, Arduino1.GND
  N3: LED1.anode, Arduino1.D13/SCK
  N4: LED2.anode, Arduino1.D12/MISO
  N5: LED3.anode, Arduino1.D11_PWM/MOSI
  N6: LED4.cathode, LED5.cathode, LED6.cathode, R2.Pin_1
  N7: LED4.anode, Arduino1.D10_PWM/SS
  N8: LED5.anode, Arduino1.D9_PWM
  N9: LED6.anode, Arduino1.D8

notes:
  Fun with Arduino by Rob Purser is licensed under a
  Creative Commons
  Attribution-NonCommercial-ShareAlike 3.0 Unported License.
  Based on a work at https://sites.google.com/site/funarduino/
