# Fritzing sketch Traffic_Light_AtHome_Solution (saved by Fritzing 0.8.7b)
breadboards: 1

parts:
  R1 = Resistor [tolerance=±5% resistance=330 package=THT]
  Traffic_Light_1 = LED - 5mm [color="Red (633nm)" package="5 mm [THT]"]
  LED2 = LED - 5mm [color="Yellow (595nm)" package="5 mm [THT]"]
  LED3 = LED - 5mm [color="Green (570nm)" package="5 mm [THT]"]
  Traffic_Light_2 = LED - 5mm [color="Red (633nm)" package="5 mm [THT]"]
  LED5 = LED - 5mm [color="Yellow (595nm)" package="5 mm [THT]"]
  LED6 = LED - 5mm [color="Green (570nm)" package="5 mm [THT]"]
  R2 = Resistor [tolerance=±5% resistance=330 package=THT]
  Arduino1 = Arduino Uno (Rev3)
  Sensor_1 = Pushbutton [package="[THT]"]
  part = Arduino Uno (Rev3)  # not connected
  Sensor_2 = Pushbutton [package="[THT]"]

nets:
  N1: R1.Pin_0, Traffic_Light_1.cathode, LED2.cathode, LED3.cathode
  GND: R1.Pin_1, R2.Pin_0, Arduino1.GND, Sensor_1.Pin_3, Sensor_1.Pin_4, Sensor_2.Pin_3, Sensor_2.Pin_4
  N2: Traffic_Light_1.anode, Arduino1.D13/SCK
  N3: LED2.anode, Arduino1.D12/MISO
  N4: LED3.anode, Arduino1.D11_PWM/MOSI
  N5: Traffic_Light_2.cathode, LED5.cathode, LED6.cathode, R2.Pin_1
  N6: Traffic_Light_2.anode, Arduino1.D10_PWM/SS
  N7: LED5.anode, Arduino1.D9_PWM
  N8: LED6.anode, Arduino1.D8
  N9: Arduino1.D6_PWM, Sensor_1.Pin_2
  N10: Arduino1.D7, Sensor_2.Pin_2

notes:
  Fun with Arduino by Rob Purser is licensed under a
  Creative Commons
  Attribution-NonCommercial-ShareAlike 3.0 Unported License.
  Based on a work at https://sites.google.com/site/funarduino/
