# Fritzing sketch Traffic_Light_Delay (saved by Fritzing 0.8.7b)
breadboards: 1

parts:
  R1 = Resistor [tolerance=±5% resistance=330 package=THT]
  LED1 = LED - 5mm [color="Red (633nm)" package="5 mm [THT]"]
  LED2 = LED - 5mm [color="Yellow (595nm)" package="5 mm [THT]"]
  LED3 = LED - 5mm [color="Green (570nm)" package="5 mm [THT]"]
  LED4 = LED - 5mm [color="Red (633nm)" package="5 mm [THT]"]
  LED5 = LED - 5mm [color="Yellow (595nm)" package="5 mm [THT]"]
  LED6 = LED - 5mm [color="Green (570nm)" package="5 mm [THT]"]
  R2 = Resistor [tolerance=±5% resistance=330 package=THT]
  S2 = Pushbutton [package="[THT]"]
  R3 = Rotary Potentiometer (Small) [maximum_resistance=100kΩ package=THT]
  Arduino1 = Arduino Uno (Rev3)
  part = Arduino Uno (Rev3)  # not connected

nets:
  N1: R1.Pin_0, LED1.cathode, LED2.cathode, LED3.cathode
  GND: R1.Pin_1, R2.Pin_0, S2.Pin_4, R3.leg1, Arduino1.GND
  N2: LED1.anode, Arduino1.D13/SCK
  N3: LED2.anode, Arduino1.D12/MISO
  N4: LED3.anode, Arduino1.D11_PWM/MOSI
  N5: LED4.cathode, LED5.cathode, LED6.cathode, R2.Pin_1
  N6: LED4.anode, Arduino1.D10_PWM/SS
  N7: LED5.anode, Arduino1.D9_PWM
  N8: LED6.anode, Arduino1.D8
  N9: S2.Pin_2, Arduino1.D7
  N10: R3.wiper, Arduino1.A0
  N11: R3.leg2, Arduino1.5V

notes:
  Fun with Arduino by Rob Purser is licensed under a
  Creative Commons
  Attribution-NonCommercial-ShareAlike 3.0 Unported License.
  Based on a work at https://sites.google.com/site/funarduino/
