# Fritzing sketch Pulse_LED (saved by Fritzing 0.8.7b)
breadboards: 1

parts:
  R3 = Resistor [tolerance=±5% resistance=330 package=THT]
  LED1 = RGB LED (com. cathode, rgb) [package="5 mm [THT]"]
  part = RGB LED (com. cathode, rgb) [package="5 mm [THT]"]  # not connected
  Arduino1 = Arduino Uno (Rev3)

nets:
  N1: R3.Pin_0, LED1.blue_anode
  N2: R3.Pin_1, Arduino1.D9_PWM
  GND: LED1.common_cathode, Arduino1.GND

notes:
  Fun with Arduino by Rob Purser is licensed under a
  Creative Commons
  Attribution-NonCommercial-ShareAlike 3.0 Unported License.
  Based on a work at https://sites.google.com/site/funarduino
  Copyright 2013, Rob Purser
