# Fritzing sketch RGB_LED (saved by Fritzing 0.8.7b)
breadboards: 1

parts:
  R1 = Resistor [tolerance=±5% resistance=330 package=THT]
  R2 = Resistor [tolerance=±5% resistance=330 package=THT]
  R3 = Resistor [tolerance=±5% resistance=330 package=THT]
  LED1 = RGB LED (com. cathode, rgb) [package="5 mm [THT]"]
  part = RGB LED (com. cathode, rgb) [package="5 mm [THT]"]  # not connected
  Arduino1 = Arduino Uno (Rev3)

nets:
  N1: R1.Pin_0, LED1.red_anode
  N2: R1.Pin_1, Arduino1.D11_PWM/MOSI
  N3: R2.Pin_0, LED1.green_anode
  N4: R2.Pin_1, Arduino1.D10_PWM/SS
  N5: R3.Pin_0, LED1.blue_anode
  N6: R3.Pin_1, Arduino1.D9_PWM
  GND: LED1.common_cathode, Arduino1.GND

notes:
  Fun with Arduino by Rob Purser is licensed under a
  Creative Commons
  Attribution-NonCommercial-ShareAlike 3.0 Unported License.
  Based on a work at https://sites.google.com/site/funarduino
  Copyright 2013, Rob Purser
