# Fritzing sketch Motor_Fundamentals (saved by Fritzing 0.8.7b)
breadboards: 1

parts:
  M1 = DC Motor
  D1 = Rectifier Diode [part_number=1N4001 breakdown_voltage=3.6V package="300 mil [THT]"]
  Q1 = NPN-Transistor [package="TO92 [THT]"]
  Arduino1 = Arduino Uno (Rev3)
  part = Arduino Uno (Rev3)  # not connected

nets:
  N1: M1.pin_1, D1.anode, Q1.C
  5V: M1.pin_2, D1.cathode, Arduino1.5V
  GND: Q1.E, Arduino1.GND
  N2: Q1.B, Arduino1.D11_PWM/MOSI

notes:
  Fun with Arduino by Rob Purser is licensed under a
  Creative Commons
  Attribution-NonCommercial-ShareAlike 3.0 Unported License.
  Based on a work at https://sites.google.com/site/funarduino/
  Copyright 2013, Rob Purser
