# Fritzing sketch Servo (saved by Fritzing 0.8.7b)

parts:
  J1 = Basic Servo
  Arduino1 = Arduino Uno (Rev3)
  part = Arduino Uno (Rev3)  # not connected

nets:
  GND: J1.gnd, Arduino1.GND
  5V: J1.vcc, Arduino1.5V
  N1: J1.pulse, Arduino1.D9_PWM

notes:
  Fun with Arduino by Rob Purser is licensed under a
  Creative Commons
  Attribution-NonCommercial-ShareAlike 3.0 Unported License.
  Based on a work at https://sites.google.com/site/funarduino/
  Copyright 2013, Rob Purser
