# Fritzing sketch Flex_LED (saved by Fritzing 0.8.7b)
breadboards: 1

parts:
  R4 = Resistor [tolerance=±5% resistance=10k package=THT]
  Arduino1 = Arduino Uno (Rev3)
  R5 = Basic Flex Resistor
  LED1 = LED - 5mm [color="Red (633nm)" package="5 mm [THT]"]
  LED2 = LED - 5mm [color="Red (633nm)" package="5 mm [THT]"]
  LED3 = LED - 5mm [color="Yellow (595nm)" package="5 mm [THT]"]
  LED4 = LED - 5mm [color="Green (565nm)" package="5 mm [THT]"]
  LED5 = LED - 5mm [color="Green (565nm)" package="5 mm [THT]"]
  R6 = Resistor [tolerance=±5% resistance=330 package=THT]
  R7 = Resistor [tolerance=±5% resistance=330 package=THT]
  R8 = Resistor [tolerance=±5% resistance=330 package=THT]
  R9 = Resistor [tolerance=±5% resistance=330 package=THT]
  R10 = Resistor [tolerance=±5% resistance=330 package=THT]

nets:
  N1: R4.Pin_0, Arduino1.A0, R5.Pin_2
  N2: R4.Pin_1, Arduino1.5V
  N3: Arduino1.D9_PWM, LED2.anode
  N4: Arduino1.D10_PWM/SS, LED1.anode
  N5: Arduino1.GND, R5.pin_1, R6.Pin_1, R7.Pin_1, R8.Pin_1, R9.Pin_1, R10.Pin_1
  N6: Arduino1.D3_PWM, LED5.anode
  N7: Arduino1.D5_PWM, LED4.anode
  N8: Arduino1.D6_PWM, LED3.anode
  N9: LED1.cathode, R6.Pin_0
  N10: LED2.cathode, R7.Pin_0
  N11: LED3.cathode, R8.Pin_0
  N12: LED4.cathode, R9.Pin_0
  N13: LED5.cathode, R10.Pin_0

notes:
  Fun with Arduino by Rob Purser is licensed under a
  Creative Commons
  Attribution-NonCommercial-ShareAlike 3.0 Unported License.
  Based on a work at http://www.funwitharduino.net
